// Logisim project basic-computer.circ as structural Verilog: 3 circuits, main circuit main
module ControlUnit (
  input  [15:0] C,
  input  clock,
  input  [15:0] AC,
  output LD_AC,
  output LD_DR,
  output LD_AR,
  output LD_IR,
  output LD_PC,
  output READ,
  output INC_PC,
  output WRITE,
  output [2:0] SELECT,
  output [2:0] AL,
  output out_14,
  output out_15,
  output out_16,
  output out_17,
  output out_18,
  output out_19,
  output out_20,
  output out_21,
  output out_22
);

  wire AC__0, and_1_out, B2T3D7I_prime, B5T3D7I_prime, B5T4D7I_prime, D0, D0T4, D0T5, D1, D1T4, D1T5, D2,
       D2T4, D2T5, D3, D4, D5, D5T4, D5T5, D5T6, D6, D7, d_ff_1_q, I, I_prime, or_1_out, or_4_out, or_5_out,
       or_6_out, T9, T10, T11, T12, T13, T14, T15;
  wire [3:0] counter_1_q;

  Comparator #(.width(16)) comparator_1 (.a(AC), .b({16{1'b0}}), .eq(AC__0));  // open: gt, lt
  or or_1 (or_1_out, B2T3D7I_prime, D1T5, D2T5, D5T6, D0T5, B5T4D7I_prime, WRITE, LD_PC);
  Counter #(.width(4), .max('hf)) counter_1 (
    .count(1'b1), .Q(counter_1_q), .clk(clock), .clr(d_ff_1_q));  // open: load, D, carry
  D_Flip_Flop d_ff_1 (.clk(clock), .D(or_1_out), .Q(d_ff_1_q));  // open: Qn, preset, en, reset
  D_Flip_Flop d_ff_2 (.clk(clock), .D(C[15]), .Q(I), .Qn(I_prime), .en(out_16));  // open: preset, reset
  Decoder #(.select(4), .enable("false")) decoder_1 (
    .out0(out_14), .out1(LD_IR), .out2(out_16), .out3(out_17), .out4(out_18), .out5(out_19), .out6(out_20),
    .out7(out_21), .out8(out_22), .out9(T9), .out10(T10), .out11(T11), .out12(T12), .out13(T13), .out14(T14),
    .out15(T15), .sel(counter_1_q));
  Decoder #(.select(3), .enable("false")) decoder_2 (
    .out0(D0), .out1(D1), .out2(D2), .out3(D3), .out4(D4), .out5(D5), .out6(D6), .out7(D7), .sel(C[14:12]));
  and BUN (LD_PC, D4, out_18);
  and AND1 (D0T4, D0, out_18);
  and AND2 (D0T5, D0, out_19);
  and ADD1 (D1T4, D1, out_18);
  and ADD2 (D1T5, D1, out_19);
  and LDA1 (D2T4, D2, out_18);
  and LDA2 (D2T5, D2, out_19);
  and STA (WRITE, D3, out_18);
  and SUB1 (D5T4, D5, out_18);
  and SUB2 (D5T5, D5, out_19);
  and SUB3 (D5T6, D5, out_20);
  and INC1 (B5T3D7I_prime, C[5], out_17, D7, I_prime);
  and INC2 (B5T4D7I_prime, C[5], out_18, D7, I_prime);
  and SZA (B2T3D7I_prime, C[2], out_17, D7, I_prime);
  and and_1 (and_1_out, AC__0, B2T3D7I_prime);
  or or_2 (LD_AR, out_14, out_16);
  or or_3 (INC_PC, and_1_out, LD_IR);
  or or_4 (or_4_out, LD_IR, D0T4, D1T4, D2T4, D5T4);
  or or_5 (or_5_out, WRITE, B5T3D7I_prime, B5T4D7I_prime, D5T5);
  or or_6 (or_6_out, D5T5, D2T5, B5T3D7I_prime);
  or or_7 (LD_AC, B5T4D7I_prime, D5T6, D0T5, D1T5, B5T3D7I_prime, D2T5, D5T5);
  or or_8 (LD_DR, B5T4D7I_prime, D0T4, D1T4, D5T4, D2T4, D5T5, B5T3D7I_prime);
  Priority_Encoder priority_encoder_1 (
    .in0(or_4_out), .in1(LD_PC), .in2(1'b0), .in3(1'b0), .in4(or_5_out), .in5(out_14), .in6(out_16),
    .in7(1'b0), .out(SELECT), .en_in(1'b1));  // open: gs, en_out
  or or_9 (READ, D0T4, LD_IR, D1T4, D2T4, D5T4);
  Priority_Encoder priority_encoder_2 (
    .in0(1'b0), .in1(D1T5), .in2(D5T6), .in3(or_6_out), .in4(D0T5), .in5(1'b0), .in6(1'b0),
    .in7(B5T4D7I_prime), .out(AL), .en_in(1'b1));  // open: gs, en_out

  assign out_15 = LD_IR;

  // Other names for the same wires on the sheet: B0 = C[0]; B1 = C[1]; B2 = C[2]; B3 = C[3]; B4 = C[4]; B5 = C[5];
  //   B6 = C[6]; B7 = C[7]; B8 = C[8]; B9 = C[9]; B10 = C[10]; B11 = C[11]; D3T4 = WRITE; D4T4 = LD_PC; T0 = out_14;
  //   T1 = LD_IR; T2 = out_16; T3 = out_17; T4 = out_18; T5 = out_19; T6 = out_20; T7 = out_21; T8 = out_22
endmodule

module main (
  input  in_1,
  input  in_2,
  output out_3
);

  wire clock_1_out, d_ff_1_q, INC_PC, LD_AC, LD_AR, LD_DR, LD_IR, LD_PC, READ, WRITE;
  wire [2:0] AL, SELECT;
  wire [6:0] AR_q, bit_extender_1_out;
  wire [15:0] AC, alu_1_ac_output, bit_extender_2_out, DR_q, IR_q, multiplexer_1_out, PC_q, ram_1_data, TR_q;

  Clock clock_1 (.out(clock_1_out));
  Bit_Extender #(.in_width(16), .out_width(7)) bit_extender_1 (.in(multiplexer_1_out), .out(bit_extender_1_out));
  Register #(.width(7)) AR (.D(bit_extender_1_out), .en(LD_AR), .Q(AR_q), .clk(clock_1_out));  // open: clr
  Register #(.width(16)) TR (.D(multiplexer_1_out), .en(in_1), .Q(TR_q), .clk(clock_1_out));  // open: clr
  Register #(.width(16)) DR (.D(multiplexer_1_out), .en(LD_DR), .Q(DR_q), .clk(clock_1_out));  // open: clr
  Register #(.width(16)) u_AC (.D(alu_1_ac_output), .en(LD_AC), .Q(AC), .clk(clock_1_out));  // open: clr
  Register #(.width(16)) IR (.D(multiplexer_1_out), .en(LD_IR), .Q(IR_q), .clk(clock_1_out));  // open: clr
  ControlUnit controlunit_1 (
    .C(IR_q), .clock(clock_1_out), .AC(AC), .LD_AC(LD_AC), .LD_DR(LD_DR), .LD_AR(LD_AR), .LD_IR(LD_IR),
    .LD_PC(LD_PC), .READ(READ), .INC_PC(INC_PC), .WRITE(WRITE), .SELECT(SELECT), .AL(AL));  // open: out_14, out_15, out_16, out_17, out_18, out_19, out_20, out_21, out_22
  RAM #(.addrWidth(7), .dataWidth(16), .bus("separate")) ram_1 (
    .addr(AR_q), .din(multiplexer_1_out), .data(ram_1_data), .str(WRITE), .sel(1'b1), .clk(clock_1_out),
    .ld(READ));  // open: clr
  assign bit_extender_2_out = {{9{1'b0}}, AR_q};  // Bit_Extender bit_extender_2
  ALU alu_1 (.A(DR_q), .B(AC), .AL(AL), .E(out_3), .AC_Output(alu_1_ac_output));
  Counter #(.width(16), .max('hffff)) PC (
    .load(LD_PC), .D(multiplexer_1_out), .count(INC_PC), .Q(PC_q), .clk(clock_1_out), .clr(d_ff_1_q));  // open: carry
  D_Flip_Flop d_ff_1 (.clk(clock_1_out), .D(in_2), .Q(d_ff_1_q));  // open: Qn, preset, en, reset
  Multiplexer #(.select(3), .width(16), .enable("false")) multiplexer_1 (
    .in0(ram_1_data), .in1(bit_extender_2_out), .in2(TR_q), .in3(DR_q), .in4(AC), .in5(PC_q), .in6(IR_q),
    .in7({16{1'b0}}), .out(multiplexer_1_out), .sel(SELECT));
endmodule

module ALU (
  input  [15:0] A,
  input  [15:0] B,
  input  [2:0] AL,
  output E,
  output [15:0] AC_Output
);

  wire adder_1_cout, adder_2_cout, subtractor_1_bout;
  wire [15:0] adder_1_out, adder_2_out, and_1_out, or_1_out, subtractor_1_out, xor_1_out;

  Adder #(.width(16)) adder_1 (.a(A), .b(B), .out(adder_1_out), .cin(1'b0), .cout(adder_1_cout));
  Subtractor #(.width(16)) subtractor_1 (.a(A), .b(B), .out(subtractor_1_out), .bin(1'b0), .bout(subtractor_1_bout));
  assign and_1_out = A & B;  // AND_Gate and_1, 16 bits wide
  assign or_1_out = A | B;  // OR_Gate or_1, 16 bits wide
  assign xor_1_out = A ^ B;  // XOR_Gate xor_1, 16 bits wide
  Adder #(.width(16)) adder_2 (.a(A), .b({16{1'b0}}), .out(adder_2_out), .cin(1'b1), .cout(adder_2_cout));
  or or_2 (E, adder_1_cout, subtractor_1_bout, adder_2_cout);
  Multiplexer #(.select(3), .width(16), .enable("false")) multiplexer_1 (
    .in0({16{1'b0}}), .in1(adder_1_out), .in2(subtractor_1_out), .in3(A), .in4(and_1_out), .in5(or_1_out),
    .in6(xor_1_out), .in7(adder_2_out), .out(AC_Output), .sel(AL));
endmodule
